// Logisim project RISC-V.circ as structural Verilog: 14 circuits, main circuit main
module main (
);

  wire branch_decoder_1_out_4, button_1_out, clock_1_out, clock_2_out, controller_1_out_3,
       controller_1_out_4, controller_1_out_5, controller_1_out_6, controller_1_out_7, controller_1_out_8;
  wire [1:0] controller_1_out_9, controller_1_out_10, controller_1_out_11;
  wire [2:0] controller_1_out_12, rom_1_data_2;
  wire [3:0] alu_controller_1_out_4;
  wire [31:0] adder_1_out, alu_operation_1_out_5, imm_generation_1_i_type, imm_generation_1_s_type,
       imm_generation_1_sb_type, imm_generation_1_u_type, imm_generation_1_uj_type, multiplexer_1_out,
       multiplexer_2_out, multiplexer_3_out, multiplexer_4_out, multiplexer_5_out, multiplexer_6_out,
       ram_1_data, reg_file_1_read_data1, reg_file_1_read_data_2, register_1_q, rom_1_data;

  Multiplexer #(.select(2), .width(32)) multiplexer_1 (
    .in0(adder_1_out), .in1(imm_generation_1_u_type), .in2(imm_generation_1_uj_type),
    .in3(alu_operation_1_out_5), .out(multiplexer_1_out), .sel(controller_1_out_10));  // open: en
  Register #(.width(32)) register_1 (
    .D(multiplexer_1_out), .Q(register_1_q), .clk(clock_1_out), .clr(button_1_out));  // open: en
  Clock clock_1 (.out(clock_1_out));
  Button button_1 (.out(button_1_out));
  Adder #(.width(32)) adder_1 (.a(register_1_q), .b(32'h4), .out(adder_1_out));  // open: cin, cout
  ROM #(.addrWidth(10), .dataWidth(32)) rom_1 (
    .addr(register_1_q[11:2]), .data({rom_1_data[31:15], rom_1_data_2, rom_1_data[11:0]}));  // open: sel
  Controller controller_1 (
    .in_1(rom_1_data[6:0]), .out_3(controller_1_out_3), .out_5(controller_1_out_5),
    .out_6(controller_1_out_6), .out_7(controller_1_out_7), .out_8(controller_1_out_8),
    .out_9(controller_1_out_9), .out_10(controller_1_out_10), .out_11(controller_1_out_11),
    .out_12(controller_1_out_12), .out_4(controller_1_out_4), .in_2(branch_decoder_1_out_4));
  imm_generation imm_generation_1 (
    .instruction({rom_1_data[31:15], rom_1_data_2, rom_1_data[11:0]}), .PC(register_1_q),
    .I_TYPE(imm_generation_1_i_type), .S_TYPE(imm_generation_1_s_type), .SB_TYPE(imm_generation_1_sb_type),
    .U_TYPE(imm_generation_1_u_type), .UJ_TYPE(imm_generation_1_uj_type));
  Multiplexer #(.select(2), .width(32)) multiplexer_2 (
    .in0(imm_generation_1_i_type), .in1(imm_generation_1_s_type), .in3(imm_generation_1_sb_type),
    .out(multiplexer_2_out), .sel(controller_1_out_11));  // open: in2, en
  Reg_file reg_file_1 (
    .rd(multiplexer_6_out), .rd_sel(rom_1_data[11:7]), .read_data1(reg_file_1_read_data1),
    .read_data_2(reg_file_1_read_data_2), .rs1_sel(rom_1_data[19:15]), .rs2_sel(rom_1_data[24:20]),
    .in_6(clock_1_out), .Reset(button_1_out), .in_3(controller_1_out_7));
  Multiplexer #(.select(2), .width(32)) multiplexer_3 (
    .in0(reg_file_1_read_data1), .in1(adder_1_out), .in2(register_1_q), .out(multiplexer_3_out),
    .sel(controller_1_out_9));  // open: in3, en
  Multiplexer #(.width(32)) multiplexer_4 (
    .in0(reg_file_1_read_data_2), .in1(multiplexer_2_out), .out(multiplexer_4_out), .sel(controller_1_out_8));  // open: en
  Alu_controller alu_controller_1 (
    .ALU(controller_1_out_12), .Funct_3(rom_1_data_2), .FUNC7(rom_1_data[30]), .out_4(alu_controller_1_out_4));
  Branch_decoder branch_decoder_1 (
    .Operand_A(reg_file_1_read_data1), .Operand_B(reg_file_1_read_data_2), .out_4(branch_decoder_1_out_4),
    .in_3(rom_1_data_2));
  ALU_operation alu_operation_1 (
    .out_5(alu_operation_1_out_5), .Operand_B(multiplexer_3_out), .Operand_A(multiplexer_4_out),
    .in_3(alu_controller_1_out_4));  // open: out_4
  Clock clock_2 (.out(clock_2_out));
  RAM #(.addrWidth(10), .dataWidth(32), .bus("separate")) ram_1 (
    .addr(alu_operation_1_out_5[11:2]), .din(reg_file_1_read_data_2), .data(ram_1_data),
    .str(controller_1_out_3), .clk(clock_2_out), .ld(controller_1_out_5));  // open: sel, clr
  Multiplexer #(.width(32)) multiplexer_5 (
    .in0(alu_operation_1_out_5), .in1(ram_1_data), .out(multiplexer_5_out), .sel(controller_1_out_6));  // open: en
  Multiplexer #(.width(32)) multiplexer_6 (
    .in0(multiplexer_5_out), .in1(adder_1_out), .out(multiplexer_6_out), .sel(controller_1_out_4));  // open: en

  // Notes on the sheet:
  //   contents of rom_1 (hex, n*v repeats v):
  //   52083 452103 1b3 a203 4181b3 408093 fff10113 fe0118e3 352423
  //   Single cycle RISC V (nothing loaded in ROM)
endmodule

module Reg_file (
  input  [31:0] rd,
  input  [4:0] rs1_sel,
  input  in_3,
  input  [4:0] rd_sel,
  input  [4:0] rs2_sel,
  input  in_6,
  input  Reset,
  output [31:0] read_data1,
  output [31:0] read_data_2
);

  wire decoder_1_out0, decoder_1_out1, decoder_1_out2, decoder_1_out3, decoder_1_out4, decoder_1_out5,
       decoder_1_out6, decoder_1_out7, decoder_1_out8, decoder_1_out9, decoder_1_out10, decoder_1_out11,
       decoder_1_out12, decoder_1_out13, decoder_1_out14, decoder_1_out15, decoder_1_out16, decoder_1_out17,
       decoder_1_out18, decoder_1_out19, decoder_1_out20, decoder_1_out21, decoder_1_out22, decoder_1_out23,
       decoder_1_out24, decoder_1_out25, decoder_1_out26, decoder_1_out27, decoder_1_out28, decoder_1_out29,
       decoder_1_out30, decoder_1_out31;
  wire [31:0] register_1_q, register_2_q, register_3_q, register_4_q, register_6_q, register_7_q,
       register_8_q, register_9_q, register_10_q, register_11_q, register_12_q, register_13_q, register_14_q,
       register_15_q, register_16_q, register_17_q, register_18_q, register_19_q, register_20_q,
       register_21_q, register_22_q, register_23_q, register_24_q, register_25_q, register_26_q,
       register_27_q, register_28_q, register_29_q, register_30_q, register_31_q, register_32_q, undriven;

  Decoder #(.select(5)) decoder_1 (
    .out0(decoder_1_out0), .out1(decoder_1_out1), .out2(decoder_1_out2), .out3(decoder_1_out3),
    .out4(decoder_1_out4), .out5(decoder_1_out5), .out6(decoder_1_out6), .out7(decoder_1_out7),
    .out8(decoder_1_out8), .out9(decoder_1_out9), .out10(decoder_1_out10), .out11(decoder_1_out11),
    .out12(decoder_1_out12), .out13(decoder_1_out13), .out14(decoder_1_out14), .out15(decoder_1_out15),
    .out16(decoder_1_out16), .out17(decoder_1_out17), .out18(decoder_1_out18), .out19(decoder_1_out19),
    .out20(decoder_1_out20), .out21(decoder_1_out21), .out22(decoder_1_out22), .out23(decoder_1_out23),
    .out24(decoder_1_out24), .out25(decoder_1_out25), .out26(decoder_1_out26), .out27(decoder_1_out27),
    .out28(decoder_1_out28), .out29(decoder_1_out29), .out30(decoder_1_out30), .out31(decoder_1_out31),
    .sel(rd_sel), .en(in_3));
  Register #(.width(32)) register_1 (.D(rd), .en(decoder_1_out0), .Q(register_1_q), .clk(in_6), .clr(Reset));
  Register #(.width(32)) register_2 (.D(rd), .en(decoder_1_out1), .Q(register_2_q), .clk(in_6), .clr(Reset));
  Register #(.width(32)) register_3 (.D(rd), .en(decoder_1_out2), .Q(register_3_q), .clk(in_6), .clr(Reset));
  Register #(.width(32)) register_4 (.D(rd), .en(decoder_1_out3), .Q(register_4_q), .clk(in_6), .clr(Reset));
  Register #(.width(32)) register_5 (.D(rd), .en(decoder_1_out4), .clk(in_6), .clr(Reset));  // open: Q
  Register #(.width(32)) register_6 (.D(rd), .en(decoder_1_out5), .Q(register_6_q), .clk(in_6), .clr(Reset));
  Register #(.width(32)) register_7 (.D(rd), .en(decoder_1_out6), .Q(register_7_q), .clk(in_6), .clr(Reset));
  Register #(.width(32)) register_8 (.D(rd), .en(decoder_1_out7), .Q(register_8_q), .clk(in_6), .clr(Reset));
  Register #(.width(32)) register_9 (.D(rd), .en(decoder_1_out8), .Q(register_9_q), .clk(in_6), .clr(Reset));
  Register #(.width(32)) register_10 (.D(rd), .en(decoder_1_out9), .Q(register_10_q), .clk(in_6), .clr(Reset));
  Register #(.width(32)) register_11 (.D(rd), .en(decoder_1_out10), .Q(register_11_q), .clk(in_6), .clr(Reset));
  Register #(.width(32)) register_12 (.D(rd), .en(decoder_1_out11), .Q(register_12_q), .clk(in_6), .clr(Reset));
  Register #(.width(32)) register_13 (.D(rd), .en(decoder_1_out12), .Q(register_13_q), .clk(in_6), .clr(Reset));
  Register #(.width(32)) register_14 (.D(rd), .en(decoder_1_out13), .Q(register_14_q), .clk(in_6), .clr(Reset));
  Register #(.width(32)) register_15 (.D(rd), .en(decoder_1_out14), .Q(register_15_q), .clk(in_6), .clr(Reset));
  Register #(.width(32)) register_16 (.D(rd), .en(decoder_1_out15), .Q(register_16_q), .clk(in_6), .clr(Reset));
  Register #(.width(32)) register_17 (.D(rd), .en(decoder_1_out16), .Q(register_17_q), .clk(in_6), .clr(Reset));
  Register #(.width(32)) register_18 (.D(rd), .en(decoder_1_out17), .Q(register_18_q), .clk(in_6), .clr(Reset));
  Register #(.width(32)) register_19 (.D(rd), .en(decoder_1_out18), .Q(register_19_q), .clk(in_6), .clr(Reset));
  Register #(.width(32)) register_20 (.D(rd), .en(decoder_1_out19), .Q(register_20_q), .clk(in_6), .clr(Reset));
  Register #(.width(32)) register_21 (.D(rd), .en(decoder_1_out20), .Q(register_21_q), .clk(in_6), .clr(Reset));
  Register #(.width(32)) register_22 (.D(rd), .en(decoder_1_out21), .Q(register_22_q), .clk(in_6), .clr(Reset));
  Register #(.width(32)) register_23 (.D(rd), .en(decoder_1_out22), .Q(register_23_q), .clk(in_6), .clr(Reset));
  Register #(.width(32)) register_24 (.D(rd), .en(decoder_1_out23), .Q(register_24_q), .clk(in_6), .clr(Reset));
  Register #(.width(32)) register_25 (.D(rd), .en(decoder_1_out24), .Q(register_25_q), .clk(in_6), .clr(Reset));
  Register #(.width(32)) register_26 (.D(rd), .en(decoder_1_out25), .Q(register_26_q), .clk(in_6), .clr(Reset));
  Register #(.width(32)) register_27 (.D(rd), .en(decoder_1_out26), .Q(register_27_q), .clk(in_6), .clr(Reset));
  Register #(.width(32)) register_28 (.D(rd), .en(decoder_1_out27), .Q(register_28_q), .clk(in_6), .clr(Reset));
  Register #(.width(32)) register_29 (.D(rd), .en(decoder_1_out28), .Q(register_29_q), .clk(in_6), .clr(Reset));
  Register #(.width(32)) register_30 (.D(rd), .en(decoder_1_out29), .Q(register_30_q), .clk(in_6), .clr(Reset));
  Register #(.width(32)) register_31 (.D(rd), .en(decoder_1_out30), .Q(register_31_q), .clk(in_6), .clr(Reset));
  Register #(.width(32)) register_32 (.D(rd), .en(decoder_1_out31), .Q(register_32_q), .clk(in_6), .clr(Reset));
  Multiplexer #(.select(5), .width(32)) multiplexer_1 (
    .in0(register_1_q), .in1(register_2_q), .in2(register_3_q), .in3(register_4_q), .in4(undriven),
    .in5(register_6_q), .in6(register_7_q), .in7(register_8_q), .in8(register_9_q), .in9(register_10_q),
    .in10(register_11_q), .in11(register_12_q), .in12(register_13_q), .in13(register_14_q),
    .in14(register_15_q), .in15(register_16_q), .in16(register_17_q), .in17(register_18_q),
    .in18(register_19_q), .in19(register_20_q), .in20(register_21_q), .in21(register_22_q),
    .in22(register_23_q), .in23(register_24_q), .in24(register_25_q), .in25(register_26_q),
    .in26(register_27_q), .in27(register_28_q), .in28(register_29_q), .in29(register_30_q),
    .in30(register_31_q), .in31(register_32_q), .out(read_data1), .sel(rs1_sel));  // open: en
  Multiplexer #(.select(5), .width(32)) multiplexer_2 (
    .in0(register_1_q), .in1(register_2_q), .in2(register_3_q), .in3(register_4_q), .in4(undriven),
    .in5(register_6_q), .in6(register_7_q), .in7(register_8_q), .in8(register_9_q), .in9(register_10_q),
    .in10(register_11_q), .in11(register_12_q), .in12(register_13_q), .in13(register_14_q),
    .in14(register_15_q), .in15(register_16_q), .in16(register_17_q), .in17(register_18_q),
    .in18(register_19_q), .in19(register_20_q), .in20(register_21_q), .in21(register_22_q),
    .in22(register_24_q), .in23(register_25_q), .in24(register_26_q), .in25(register_27_q),
    .in26(register_28_q), .in27(register_29_q), .in28(register_30_q), .in29(register_31_q),
    .in30(register_32_q), .out(read_data_2), .sel(rs2_sel));  // open: in31, en

  // Notes on the sheet:
  //   Clock
endmodule

module imm_generation (
  input  [31:0] instruction,
  input  [31:0] PC,
  output [31:0] I_TYPE,
  output [31:0] S_TYPE,
  output [31:0] SB_TYPE,
  output [31:0] U_TYPE,
  output [31:0] UJ_TYPE
);

  assign I_TYPE[31:12] = {{19{1'b0}}, instruction[31]};  // Bit_Extender bit_extender_1
  Adder #(.width(32)) adder_1 (
    .a({I_TYPE[31:12], instruction[31:25], instruction[7], instruction[11:8]}), .b(PC), .out(SB_TYPE));  // open: cin, cout
  Adder #(.width(32)) adder_2 (
    .a(PC), .b({I_TYPE[23:12], instruction[31], instruction[19:12], instruction[20], instruction[30:21]}),
    .out(UJ_TYPE));  // open: cin, cout

  assign I_TYPE[11:0] = instruction[31:20];
  assign S_TYPE = {I_TYPE[31:12], instruction[31:25], instruction[11:7]};
  assign U_TYPE = {I_TYPE[23:12], instruction[31:12]};
endmodule

module Opcode_comparator (
  input  [6:0] in_1,
  output out_2,
  output out_3,
  output out_4,
  output out_5,
  output out_6,
  output out_7,
  output out_8,
  output out_9,
  output out_10
);

  Comparator #(.width(7)) comparator_1 (.a(7'b0110011), .b(in_1), .eq(out_2));  // open: gt, lt
  Comparator #(.width(7)) comparator_2 (.a(7'b0010011), .b(in_1), .eq(out_3));  // open: gt, lt
  Comparator #(.width(7)) comparator_3 (.a(7'b0100011), .b(in_1), .eq(out_4));  // open: gt, lt
  Comparator #(.width(7)) comparator_4 (.a(7'b0110111), .b(in_1), .eq(out_5));  // open: gt, lt
  Comparator #(.width(7)) comparator_5 (.a(7'b0010111), .b(in_1), .eq(out_6));  // open: gt, lt
  Comparator #(.width(7)) comparator_6 (.a(7'b1100011), .b(in_1), .eq(out_7));  // open: gt, lt
  Comparator #(.width(7)) comparator_7 (.a(7'b1100111), .b(in_1), .eq(out_8));  // open: gt, lt
  Comparator #(.width(7)) comparator_8 (.a(7'b0000011), .b(in_1), .eq(out_9));  // open: gt, lt
  Comparator #(.width(7)) comparator_9 (.a(7'b1101111), .b(in_1), .eq(out_10));  // open: gt, lt

  // Notes on the sheet:
  //   lui
  //   auiPC
  //   B
  //   JALR
  //   LW
  //   JAL
  //   R
  //   I
  //   S
endmodule

module PC_sel (
  input  B,
  input  JAL,
  input  JALR,
  output [1:0] out_4
);

  wire and_1_out, and_2_out, and_3_out, and_4_out, not_1_out, not_2_out, not_3_out, not_4_out, not_5_out,
       not_6_out, not_7_out, not_8_out;

  not not_1 (not_1_out, B);
  not not_2 (not_2_out, JAL);
  not not_3 (not_3_out, B);
  not not_4 (not_4_out, JALR);
  not not_5 (not_5_out, B);
  not not_6 (not_6_out, JAL);
  not not_7 (not_7_out, JAL);
  not not_8 (not_8_out, JALR);
  and and_1 (and_1_out, not_1_out, not_2_out, JALR);
  and and_2 (and_2_out, not_3_out, JAL, not_4_out);
  and and_3 (and_3_out, not_5_out, not_6_out, JALR);
  and and_4 (and_4_out, B, not_7_out, not_8_out);
  or or_1 (out_4[1], and_1_out, and_2_out);
  or or_2 (out_4[0], and_3_out, and_4_out);
endmodule

module program_counter (
  output [31:0] out_1
);

  wire button_1_out, clock_1_out;
  wire [9:0] register_1_q_2;
  wire [31:0] adder_1_out, register_1_q;

  Clock clock_1 (.out(clock_1_out));
  Register #(.width(32)) register_1 (
    .D(adder_1_out), .Q({register_1_q[31:12], register_1_q_2, register_1_q[1:0]}), .clk(clock_1_out),
    .clr(button_1_out));  // open: en
  Button button_1 (.out(button_1_out));
  Adder #(.width(32)) adder_1 (
    .a({register_1_q[31:12], register_1_q_2, register_1_q[1:0]}), .b(32'h4), .out(adder_1_out));  // open: cin, cout
  ROM #(.addrWidth(10), .dataWidth(32)) rom_1 (.addr(register_1_q_2), .data(out_1));  // open: sel

  // Notes on the sheet:
  //   contents of rom_1 (hex, n*v repeats v):
  //   300513 400593 b50633
endmodule

module opA_sel (
  input  lui,
  input  auiPC,
  input  JAL,
  output [1:0] out_4
);

  wire and_1_out, and_2_out, and_3_out, and_4_out, not_1_out, not_2_out, not_3_out, not_4_out, not_5_out,
       not_6_out, not_7_out, not_8_out;

  not not_1 (not_1_out, lui);
  not not_2 (not_2_out, auiPC);
  not not_3 (not_3_out, auiPC);
  not not_4 (not_4_out, JAL);
  not not_5 (not_5_out, lui);
  not not_6 (not_6_out, JAL);
  not not_7 (not_7_out, auiPC);
  not not_8 (not_8_out, JAL);
  and and_1 (and_1_out, not_1_out, not_2_out, JAL);
  and and_2 (and_2_out, lui, not_3_out, not_4_out);
  and and_3 (and_3_out, not_5_out, auiPC, not_6_out);
  and and_4 (and_4_out, lui, not_7_out, not_8_out);
  or or_1 (out_4[1], and_1_out, and_2_out);
  or or_2 (out_4[0], and_3_out, and_4_out);
endmodule

module control_decode (
  input  B_new,
  input  R,
  input  I,
  input  S,
  input  lui,
  input  auiPC,
  input  JAL,
  input  JALR,
  input  lw,
  input  B,
  output JALR_2,
  output Mem_Write,
  output Mem_Read,
  output Write_Back,
  output Reg_en,
  output opB_sel,
  output [1:0] opA_sel,
  output [1:0] PC_sel,
  output [1:0] imm_sel,
  output [2:0] ALU_op
);

  wire and_1_out;

  and and_1 (and_1_out, B_new, B);
  or or_1 (Reg_en, R, I, lui, auiPC, JAL, JALR, lw);
  or or_2 (opB_sel, I, S, lui, auiPC, JALR, lw);
  opA_sel opa_sel_1 (.lui(lui), .auiPC(auiPC), .JAL(JALR), .out_4(opA_sel));
  PC_sel pc_sel_1 (.B(and_1_out), .JAL(JAL), .JALR(JALR), .out_4(PC_sel));
  imm_sel imm_sel_1 (.R(R), .S(S), .B(and_1_out), .lui(lui), .auiPC(auiPC), .JAL(JAL), .out_7(imm_sel));
  ALU_op alu_op_1 (.I(I), .S(S), .auiPC(auiPC), .lui(lui), .lw(lw), .JALR(JALR), .JAL(JAL), .out_8(ALU_op));

  assign JALR_2 = JALR;
  assign Mem_Read = lw;
  assign Mem_Write = S;
  assign Write_Back = lw;
endmodule

module Alu_controller (
  input  [2:0] ALU,
  input  [2:0] Funct_3,
  input  FUNC7,
  output [3:0] out_4
);

  wire and_1_out, and_2_out, and_3_out, and_4_out, and_5_out, and_6_out, and_7_out, and_8_out, and_9_out,
       and_10_out, and_11_out, and_12_out, and_13_out, and_14_out, not_1_out, not_2_out, not_3_out,
       not_4_out, not_5_out, not_6_out, not_7_out, not_8_out, not_9_out, not_10_out, not_11_out, not_12_out;

  not not_1 (not_1_out, ALU[2]);
  not not_2 (not_2_out, ALU[0]);
  not not_3 (not_3_out, Funct_3[2]);
  not not_4 (not_4_out, Funct_3[1]);
  and and_1 (and_1_out, not_4_out, Funct_3[0]);
  and and_2 (and_2_out, Funct_3[2], not_5_out);
  not not_5 (not_5_out, Funct_3[1]);
  and and_3 (and_3_out, ALU[2], ALU[1]);
  not not_6 (not_6_out, Funct_3[2]);
  and and_4 (and_4_out, not_6_out, not_7_out, Funct_3[0]);
  not not_7 (not_7_out, Funct_3[1]);
  and and_5 (and_5_out, Funct_3[2], FUNC7);
  and and_6 (and_6_out, Funct_3[2], Funct_3[1]);
  and and_7 (and_7_out, ALU[2], ALU[1]);
  not not_8 (not_8_out, Funct_3[2]);
  and and_8 (and_8_out, not_8_out, FUNC7);
  not not_9 (not_9_out, Funct_3[2]);
  and and_9 (and_9_out, not_9_out, Funct_3[0]);
  not not_10 (not_10_out, Funct_3[1]);
  and and_10 (and_10_out, not_10_out, Funct_3[0], not_11_out);
  not not_11 (not_11_out, FUNC7);
  and and_11 (and_11_out, Funct_3[2], Funct_3[1], not_12_out);
  not not_12 (not_12_out, Funct_3[0]);
  and and_12 (and_12_out, ALU[2], ALU[1], ALU[0]);
  and and_13 (and_13_out, not_1_out, not_2_out, not_3_out, Funct_3[1]);
  or or_1 (out_4[3], and_13_out, and_14_out);
  and and_14 (and_14_out, ALU[2], ALU[1]);
  or or_2 (out_4[2], and_1_out, and_2_out, and_3_out);
  or or_3 (out_4[1], and_4_out, and_5_out, and_6_out, and_7_out);
  or or_4 (out_4[0], and_8_out, and_9_out, and_10_out, and_11_out, and_12_out);
endmodule

module ALU_operation (
  input  [31:0] Operand_B,
  input  [31:0] Operand_A,
  input  [3:0] in_3,
  output out_4,
  output [31:0] out_5
);

  wire comparator_1_lt;
  wire [31:0] _0010_out, _0011_out, _0110_out, adder_1_out, multiplexer_1_out, shifter_1_out, shifter_2_out,
       shifter_3_out, subtractor_1_out;

  Adder #(.width(32)) adder_1 (.a(Operand_A), .b(Operand_B), .out(adder_1_out), .cout(out_4));  // open: cin
  Subtractor #(.width(32)) subtractor_1 (.a(Operand_A), .b(Operand_B), .out(subtractor_1_out));  // open: bin, bout
  assign _0010_out = Operand_A & Operand_B;  // AND_Gate _0010, 32 bits wide
  assign _0011_out = Operand_A | Operand_B;  // OR_Gate _0011, 32 bits wide
  Shifter #(.width(32)) shifter_1 (.in(Operand_A), .\dist (Operand_B[4:0]), .out(shifter_1_out));
  Shifter #(.width(32), .shift("lr")) shifter_2 (.in(Operand_A), .\dist (Operand_B[4:0]), .out(shifter_2_out));
  Shifter #(.width(32), .shift("ar")) shifter_3 (.in(Operand_A), .\dist (Operand_B[4:0]), .out(shifter_3_out));
  Comparator #(.width(32)) comparator_1 (.a(Operand_A), .b(Operand_B), .lt(comparator_1_lt));  // open: gt, eq
  assign _0110_out = Operand_A ^ Operand_B;  // XOR_Gate _0110, 32 bits wide
  Multiplexer #(.width(32)) multiplexer_1 (
    .in1(32'h1), .out(multiplexer_1_out), .sel(comparator_1_lt));  // open: in0, en
  Multiplexer #(.select(4), .width(32)) multiplexer_2 (
    .in0(adder_1_out), .in1(subtractor_1_out), .in2(_0010_out), .in3(_0011_out), .in4(_0110_out),
    .in5(shifter_1_out), .in6(shifter_2_out), .in7(shifter_3_out), .in8(multiplexer_1_out), .out(out_5),
    .sel(in_3));  // open: in9, in10, in11, in12, in13, in14, in15, en
endmodule

module Branch_decoder (
  input  [31:0] Operand_A,
  input  [31:0] Operand_B,
  input  [2:0] in_3,
  output out_4
);

  wire comparator_1_eq, comparator_1_gt, comparator_1_lt, comparator_2_gt, comparator_2_lt, not_1_out,
       or_1_out;

  Comparator #(.width(32)) comparator_1 (
    .a(Operand_A), .b(Operand_B), .gt(comparator_1_gt), .eq(comparator_1_eq), .lt(comparator_1_lt));
  Comparator #(.width(32)) comparator_2 (
    .a(Operand_A), .b(Operand_B), .gt(comparator_2_gt), .lt(comparator_2_lt));  // open: eq
  not not_1 (not_1_out, comparator_1_eq);
  or or_1 (or_1_out, comparator_1_gt, comparator_1_eq);
  Multiplexer #(.select(3)) multiplexer_1 (
    .in0(comparator_1_eq), .in1(not_1_out), .in4(comparator_1_lt), .in5(or_1_out), .in6(comparator_2_lt),
    .in7(comparator_2_gt), .out(out_4), .sel(in_3));  // open: in2, in3, en
endmodule

module imm_sel (
  input  R,
  input  S,
  input  B,
  input  lui,
  input  auiPC,
  input  JAL,
  output [1:0] out_7
);

  wire and_1_out, and_2_out, and_3_out, and_4_out, and_5_out, and_6_out, and_7_out, and_8_out, and_9_out,
       not_1_out, not_2_out, not_3_out, not_4_out, not_5_out, not_6_out, not_7_out, not_8_out, not_9_out,
       not_10_out, not_11_out, not_12_out, not_13_out, not_14_out, not_15_out, not_16_out, not_17_out,
       not_18_out, not_19_out, not_20_out, not_21_out, not_22_out, not_23_out, not_24_out, not_25_out,
       not_26_out, not_27_out, not_28_out, not_29_out, not_30_out, not_31_out, not_32_out, not_33_out,
       not_34_out, not_35_out, not_36_out, not_37_out, not_38_out, not_39_out, not_40_out, not_41_out,
       not_42_out, not_43_out, not_44_out, not_45_out;

  not not_1 (not_1_out, R);
  not not_2 (not_2_out, S);
  not not_3 (not_3_out, B);
  not not_4 (not_4_out, lui);
  not not_5 (not_5_out, auiPC);
  not not_6 (not_6_out, R);
  not not_7 (not_7_out, S);
  not not_8 (not_8_out, B);
  not not_9 (not_9_out, lui);
  not not_10 (not_10_out, JAL);
  not not_11 (not_11_out, R);
  not not_12 (not_12_out, S);
  not not_13 (not_13_out, B);
  not not_14 (not_14_out, auiPC);
  not not_15 (not_15_out, JAL);
  not not_16 (not_16_out, R);
  not not_17 (not_17_out, S);
  not not_18 (not_18_out, lui);
  not not_19 (not_19_out, auiPC);
  not not_20 (not_20_out, JAL);
  not not_21 (not_21_out, S);
  not not_22 (not_22_out, B);
  not not_23 (not_23_out, lui);
  not not_24 (not_24_out, auiPC);
  not not_25 (not_25_out, JAL);
  not not_26 (not_26_out, R);
  not not_27 (not_27_out, S);
  not not_28 (not_28_out, B);
  not not_29 (not_29_out, lui);
  not not_30 (not_30_out, auiPC);
  not not_31 (not_31_out, R);
  not not_32 (not_32_out, S);
  not not_33 (not_33_out, lui);
  not not_34 (not_34_out, auiPC);
  not not_35 (not_35_out, JAL);
  not not_36 (not_36_out, R);
  not not_37 (not_37_out, B);
  not not_38 (not_38_out, lui);
  not not_39 (not_39_out, auiPC);
  not not_40 (not_40_out, JAL);
  not not_41 (not_41_out, S);
  not not_42 (not_42_out, B);
  not not_43 (not_43_out, lui);
  not not_44 (not_44_out, auiPC);
  not not_45 (not_45_out, JAL);
  and and_1 (and_1_out, not_1_out, not_2_out, not_3_out, not_4_out, not_5_out, JAL);
  and and_2 (and_2_out, not_6_out, not_7_out, not_8_out, not_9_out, auiPC, not_10_out);
  and and_3 (and_3_out, not_11_out, not_12_out, not_13_out, lui, not_14_out, not_15_out);
  and and_4 (and_4_out, not_16_out, not_17_out, B, not_18_out, not_19_out, not_20_out);
  and and_5 (and_5_out, R, not_21_out, not_22_out, not_23_out, not_24_out, not_25_out);
  and and_6 (and_6_out, not_26_out, not_27_out, not_28_out, not_29_out, not_30_out, JAL);
  and and_7 (and_7_out, not_31_out, not_32_out, B, not_33_out, not_34_out, not_35_out);
  and and_8 (and_8_out, not_36_out, S, not_37_out, not_38_out, not_39_out, not_40_out);
  and and_9 (and_9_out, R, not_41_out, not_42_out, not_43_out, not_44_out, not_45_out);
  or or_1 (out_7[1], and_1_out, and_2_out, and_3_out, and_4_out, and_5_out);
  or or_2 (out_7[0], and_6_out, and_7_out, and_8_out, and_9_out);
endmodule

module Controller (
  input  [6:0] in_1,
  input  in_2,
  output out_3,
  output out_4,
  output out_5,
  output out_6,
  output out_7,
  output out_8,
  output [1:0] out_9,
  output [1:0] out_10,
  output [1:0] out_11,
  output [2:0] out_12
);

  wire opcode_comparator_1_out_2, opcode_comparator_1_out_3, opcode_comparator_1_out_4,
       opcode_comparator_1_out_5, opcode_comparator_1_out_6, opcode_comparator_1_out_7,
       opcode_comparator_1_out_8, opcode_comparator_1_out_9, opcode_comparator_1_out_10;

  Opcode_comparator opcode_comparator_1 (
    .in_1(in_1), .out_2(opcode_comparator_1_out_2), .out_3(opcode_comparator_1_out_3),
    .out_4(opcode_comparator_1_out_4), .out_5(opcode_comparator_1_out_5), .out_6(opcode_comparator_1_out_6),
    .out_7(opcode_comparator_1_out_7), .out_8(opcode_comparator_1_out_8), .out_9(opcode_comparator_1_out_9),
    .out_10(opcode_comparator_1_out_10));
  control_decode control_decode_1 (
    .B_new(in_2), .R(opcode_comparator_1_out_2), .I(opcode_comparator_1_out_3),
    .S(opcode_comparator_1_out_4), .lui(opcode_comparator_1_out_5), .auiPC(opcode_comparator_1_out_6),
    .JAL(opcode_comparator_1_out_10), .JALR(opcode_comparator_1_out_8), .lw(opcode_comparator_1_out_9),
    .JALR_2(out_3), .Mem_Write(out_4), .Mem_Read(out_5), .Write_Back(out_6), .Reg_en(out_7), .opB_sel(out_8),
    .opA_sel(out_9), .PC_sel(out_10), .imm_sel(out_11), .ALU_op(out_12), .B(opcode_comparator_1_out_7));
endmodule

module ALU_op (
  input  I,
  input  S,
  input  auiPC,
  input  lui,
  input  lw,
  input  JALR,
  input  JAL,
  output [2:0] out_8
);

  wire and_1_out, and_2_out, and_3_out, and_4_out, and_5_out, and_6_out, and_7_out, and_8_out, and_9_out,
       and_10_out, and_11_out, and_12_out, and_13_out, not_1_out, not_2_out, not_3_out, not_4_out, not_5_out,
       not_6_out, not_7_out, not_8_out, not_9_out, not_10_out, not_11_out, not_12_out, not_13_out,
       not_14_out, not_15_out, not_16_out, not_17_out, not_18_out, not_19_out, not_20_out, not_21_out,
       not_22_out, not_23_out, not_24_out, not_25_out, not_26_out, not_27_out, not_28_out, not_29_out,
       not_30_out, not_31_out, not_32_out, not_33_out, not_34_out, not_35_out, not_36_out, not_37_out,
       not_38_out, not_39_out, not_40_out, not_41_out, not_42_out, not_43_out, not_44_out, not_45_out,
       not_46_out, not_47_out, not_48_out, not_49_out, not_50_out, not_51_out, not_52_out, not_53_out,
       not_54_out, not_55_out, not_56_out, not_57_out, not_58_out, not_59_out, not_60_out, not_61_out,
       not_62_out, not_63_out, not_64_out, not_65_out, not_66_out, not_67_out, not_68_out, not_69_out,
       not_70_out, not_71_out, not_72_out, not_73_out, not_74_out, not_75_out, not_76_out;

  not not_1 (not_1_out, I);
  not not_2 (not_2_out, S);
  not not_3 (not_3_out, auiPC);
  not not_4 (not_4_out, lui);
  not not_5 (not_5_out, lw);
  not not_6 (not_6_out, JALR);
  not not_7 (not_7_out, I);
  not not_8 (not_8_out, S);
  not not_9 (not_9_out, auiPC);
  not not_10 (not_10_out, lw);
  not not_11 (not_11_out, JALR);
  not not_12 (not_12_out, JAL);
  not not_13 (not_13_out, I);
  not not_14 (not_14_out, S);
  not not_15 (not_15_out, lui);
  not not_16 (not_16_out, lw);
  not not_17 (not_17_out, JALR);
  not not_18 (not_18_out, JAL);
  not not_19 (not_19_out, I);
  not not_20 (not_20_out, auiPC);
  not not_21 (not_21_out, lui);
  not not_22 (not_22_out, lw);
  not not_23 (not_23_out, JALR);
  not not_24 (not_24_out, JAL);
  not not_25 (not_25_out, I);
  not not_26 (not_26_out, S);
  not not_27 (not_27_out, auiPC);
  not not_28 (not_28_out, lui);
  not not_29 (not_29_out, lw);
  not not_30 (not_30_out, JALR);
  not not_31 (not_31_out, I);
  not not_32 (not_32_out, S);
  not not_33 (not_33_out, auiPC);
  not not_34 (not_34_out, lui);
  not not_35 (not_35_out, lw);
  not not_36 (not_36_out, JAL);
  not not_37 (not_37_out, I);
  not not_38 (not_38_out, S);
  not not_39 (not_39_out, auiPC);
  not not_40 (not_40_out, lw);
  not not_41 (not_41_out, JALR);
  not not_42 (not_42_out, JAL);
  not not_43 (not_43_out, S);
  not not_44 (not_44_out, auiPC);
  not not_45 (not_45_out, lui);
  not not_46 (not_46_out, lw);
  not not_47 (not_47_out, JALR);
  not not_48 (not_48_out, JAL);
  not not_49 (not_49_out, I);
  not not_50 (not_50_out, S);
  not not_51 (not_51_out, auiPC);
  not not_52 (not_52_out, lui);
  not not_53 (not_53_out, lw);
  not not_54 (not_54_out, JALR);
  not not_55 (not_55_out, I);
  not not_56 (not_56_out, S);
  not not_57 (not_57_out, auiPC);
  not not_58 (not_58_out, lui);
  not not_59 (not_59_out, lw);
  not not_60 (not_60_out, JAL);
  not not_61 (not_61_out, I);
  not not_62 (not_62_out, S);
  not not_63 (not_63_out, auiPC);
  not not_64 (not_64_out, lui);
  not not_65 (not_65_out, JALR);
  not not_66 (not_66_out, JAL);
  not not_67 (not_67_out, I);
  not not_68 (not_68_out, S);
  not not_69 (not_69_out, lui);
  not not_70 (not_70_out, lw);
  not not_71 (not_71_out, JALR);
  not not_72 (not_72_out, JAL);
  not not_73 (not_73_out, I);
  not not_74 (not_74_out, auiPC);
  not not_75 (not_75_out, lui);
  not not_76 (not_76_out, JAL);
  and and_1 (and_1_out, not_1_out, not_2_out, not_3_out, not_4_out, not_5_out, not_6_out, JAL);
  and and_2 (and_2_out, not_7_out, not_8_out, not_9_out, lui, not_10_out, not_11_out, not_12_out);
  and and_3 (and_3_out, not_13_out, not_14_out, auiPC, not_15_out, not_16_out, not_17_out, not_18_out);
  and and_4 (and_4_out, not_19_out, S, not_20_out, not_21_out, not_22_out, not_23_out, not_24_out);
  and and_5 (and_5_out, not_25_out, not_26_out, not_27_out, not_28_out, not_29_out, not_30_out, JAL);
  and and_6 (and_6_out, not_31_out, not_32_out, not_33_out, not_34_out, not_35_out, JALR, not_36_out);
  and and_7 (and_7_out, not_37_out, not_38_out, not_39_out, lui, not_40_out, not_41_out, not_42_out);
  and and_8 (and_8_out, I, not_43_out, not_44_out, not_45_out, not_46_out, not_47_out, not_48_out);
  and and_9 (and_9_out, not_49_out, not_50_out, not_51_out, not_52_out, not_53_out, not_54_out, JAL);
  and and_10 (and_10_out, not_55_out, not_56_out, not_57_out, not_58_out, not_59_out, JALR, not_60_out);
  and and_11 (and_11_out, not_61_out, not_62_out, not_63_out, not_64_out, lw, not_65_out, not_66_out);
  and and_12 (and_12_out, not_67_out, not_68_out, auiPC, not_69_out, not_70_out, not_71_out, not_72_out);
  and and_13 (and_13_out, not_73_out, S, not_74_out, not_75_out, lw, JALR, not_76_out);
  or or_1 (out_8[2], and_1_out, and_2_out, and_3_out, and_4_out);
  or or_2 (out_8[1], and_5_out, and_6_out, and_7_out, and_8_out);
  or or_3 (out_8[0], and_9_out, and_10_out, and_11_out, and_12_out, and_13_out);
endmodule
